# Fritzing sketch sketch (saved by Fritzing 0.9.2b)
circuit board: 8.46667cm x 5.64444cm
breadboards: 1

parts:
  part = Arduino Uno (Rev3)
  Bluetooth_for_connection = Bluetooth HC-06
  Bluetooth_for_detection = Bluetooth HC-06
  R1 = Resistor [tolerance=±5% resistance=220 package=THT]
  R2 = Resistor [tolerance=±5% resistance=220 package=THT]
  R3 = Resistor [tolerance=±5% resistance=220 package=THT]
  LED1 = LED - 5mm [color="Red (633nm)" package="5 mm [THT]"]
  LED2 = LED - 5mm [color="Yellow (595nm)" package="5 mm [THT]"]
  LED3 = LED - 5mm [color="Green (560nm)" package="5 mm [THT]"]
  VCC1 = Battery block 9V
  RING_button = Pushbutton [package="[THT]"]
  R4 = Resistor [tolerance=±5% resistance=10k package=THT]
  Buzzer = Piezo Speaker

nets:
  N1: part.D10_PWM/SS, R3.Pin_0
  N2: part.D11_PWM/MOSI, R2.Pin_0
  N3: part.D12/MISO, R1.Pin_0
  N4: part.D1/TX, Bluetooth_for_connection.RXD
  N5: part.D4, Bluetooth_for_connection.TXD
  N6: part.D6_PWM, Buzzer.pin2
  N7: part.D7, RING_button.Pin_1, RING_button.Pin_2, R4.Pin_0
  VCC: part.5V, Bluetooth_for_connection.VCC, Bluetooth_for_detection.VCC, RING_button.Pin_3, RING_button.Pin_4
  GND: part.GND, Bluetooth_for_connection.GND, Bluetooth_for_detection.GND, LED1.anode, LED2.anode, LED3.anode, VCC1.-, R4.Pin_1, Buzzer.pin1
  N8: part.VIN, VCC1.+
  N9: R1.Pin_1, LED3.cathode
  N10: R2.Pin_1, LED2.cathode
  N11: R3.Pin_1, LED1.cathode
